# Fritzing sketch Umbrella_Rent_System_회로 (saved by Fritzing 0.9.10b)
breadboards: 1

parts:
  부품1 = Arduino Uno (Rev3)
  부품2 = Bluetooth HC-05 Macho
  J1 = Basic Servo
  J2 = Infrared Proximity Sensor [distance_to_obstacle=50%]
  J3 = Basic Servo

nets:
  N1: 부품1.D8, J1.pulse
  N2: 부품1.D9_PWM, J3.pulse
  GND: 부품1.GND, 부품2.GND, J1.gnd, J2.GND, J3.gnd
  N3: 부품1.D2, J2.Vout
  N4: 부품1.D3_PWM, 부품2.RXD
  N5: 부품1.D4, 부품2.TXD
  VCC: 부품1.5V, 부품2.VCC, J1.vcc, J2.Vcc, J3.vcc

// code stored in the sketch: Untitled2.ino
#include  <Servo.h>

Servo servo_test;        //initialize a servo object for the connected servo  
                
int angle = 90;
int command;

#define potPin A0 
int potValue = 0;

int T = 2; 

void setup()
{
 Serial.begin(9600); 
 pinMode(T, INPUT);
servo_test.attach(9);
}

void loop()
{
if (Serial.available() > 0) {
    command = Serial.read();
  }
 if (LOW == digitalRead(T))
 {
 Serial.println("IR Detected"); //detected

 }
 else
 {
 Serial.print("."); 
 digitalWrite(LED, LOW);
 }
 delay(100);
}
